// Logisim project CPU(S-MIPS).circ as structural Verilog: 1 circuit, main circuit S-MIPS
module S_MIPS (
  input  [31:0] RAM_Out_0,
  input  [31:0] RAM_Out_1,
  input  [31:0] RAM_Out_2,
  input  [31:0] RAM_Out_3,
  input  [3:0] Read_Time,
  input  [3:0] Write_Time,
  input  Reset,
  input  Clock,
  input  Kbd_Available,
  input  [6:0] Kbd_ASCII_Data,
  output [31:0] RAM_In_0,
  output [31:0] RAM_In_1,
  output [31:0] RAM_In_2,
  output [31:0] RAM_In_3,
  output Halt,
  output [15:0] Address,
  output Kbd_Enable,
  output Kbd_Clear,
  output TTY_Enable,
  output [6:0] TTY_ASCII_Data,
  output [3:0] Mask,
  output nRead_Write,
  output Chip_Select
);

  wire Fetch, Ram_Ready, ReadIns, rnd_kbd;
  wire [2:0] S_FC;
  wire [3:0] ALU_OP;
  wire [5:0] FuncCode, OpCode;
  wire [17:0] SelectorCodes;
  wire [31:0] inst, MemoryAddress, MemoryData, Out_Word;

  Control_Unit control_unit_1 (
    .START(Reset), .fetch(Fetch), .FuncCode(FuncCode), .OpCode(OpCode), .FC_Selector(S_FC), .ALU_Op(ALU_OP),
    .SelectorCodes(SelectorCodes), .rnd_kbd_Selector(rnd_kbd), .TTY_Enable(TTY_Enable),
    .ReadInstruction(ReadIns), .ChipSelect(Chip_Select), .R_W(nRead_Write), .RamReady(Ram_Ready),
    .halt(Halt), .Clock(Clock), .kbd_Enable(Reset));  // open: RESET
  Memory_Controller memory_controller_1 (
    .Input_Word(MemoryData), .O0(RAM_Out_0), .O1(RAM_Out_1), .O2(RAM_Out_2), .O3(RAM_Out_3),
    .R_W(nRead_Write), .Chip_Select(Chip_Select), .Read_Time(Read_Time), .Write_Time(Write_Time),
    .Address(Address), .OW_Out_Word(Out_Word), .Mask(Mask), .I0(RAM_In_0), .I1(RAM_In_1), .I2(RAM_In_2),
    .I3(RAM_In_3), .Ram_Ready(Ram_Ready), .MemoryAddress(MemoryAddress), .reset(Reset), .clk(Clock));
  // DataPath datapath_1: pin names not known; wires that end beside it: Reset, Out_Word, inst, Kbd_ASCII_Data, Kbd_Available, Fetch, ReadIns, SelectorCodes, rnd_kbd, ALU_OP, S_FC, Clock, MemoryAddress, TTY_ASCII_Data, FuncCode, OpCode, MemoryData

  // Other names for the same wires on the sheet: CLK = Clock; CS = Chip_Select; KBD_AVAIL = Kbd_Available;
  //   KBD_CLR = Kbd_Clear; KBD_DATA[6:0] = Kbd_ASCII_Data; RAM_A[15:0] = Address; RAM_MASK[3:0] = Mask;
  //   RI0[31:0] = RAM_In_0; RI1[31:0] = RAM_In_1; RI2[31:0] = RAM_In_2; RI_3[31:0] = RAM_In_3; RO0[31:0] = RAM_Out_0;
  //   RO1[31:0] = RAM_Out_1; RO2[31:0] = RAM_Out_2; RO3[31:0] = RAM_Out_3; RST = Reset; RW = nRead_Write;
  //   TTY_DATA[6:0] = TTY_ASCII_Data

  // Notes on the sheet:
  //   RAM TIMING
  //   KEYBOARD
  //   DATA FROM RAM
  //   RAM ADDRESS
  //   KEYBOARD
  //   TTY
  //   DATA WRITE MASK
  //   RAM CONTROL
  //   DATA TO RAM
endmodule
