// Logisim project DataPath.circ as structural Verilog: 1 circuit, main circuit DataPath
module DataPath (
  input  [31:0] Instruction,
  input  KBD_Enable,
  input  [6:0] KBD_Data,
  input  fetch,
  input  reset,
  input  S_SI,
  output [31:0] PC_Addrs,
  output TTY_Enable,
  output [6:0] TTY_Data,
  output fetched,
  output halt
);

  wire A____B, A____B_t, A___B_signed, A___B_signed_t, A___B_unsigned, B_Cero, clk, comparator_1_eq, EI, FC,
       Jmp, KBD_En, Load, mf_Hi_Lo, R_Hi_Lo, R_W, S_SB, Store, Upd_Hi, UpdateHi, W_SOU_Data;
  wire [1:0] Esp_Ins_S, S_ALUB, S_DA, S_DATA_IN, S_jmp_address;
  wire [2:0] S_FlagCondition;
  wire [3:0] Op;
  wire [4:0] DA, Rd, Rt, SA, SB;
  wire [6:0] TTY_Data_t;
  wire [15:0] Const;
  wire [25:0] dest;
  wire [31:0] ALU_Out, B, B_prime, bit_extender_3_out, Const_extended, DATA_HI, DATA_HI_LO, DATA_IN,
       DATA_INPUT, DATA_LO, Hi, jmp_address, JS, Lo, multiplexer_6_out, multiplexer_10_out, NI, random_1_out,
       SOU_Data, Special_Ins_Data;
  wire [31:7] A;

  Clock clock_1 (.out(clk));
  Multiplexer #(.width(5), .enable("false")) multiplexer_1 (.in0(Rt), .in1({5{1'b0}}), .out(SB), .sel(S_SB));
  Multiplexer #(.select(2), .width(5), .enable("false")) multiplexer_2 (
    .in0(Rd), .in1(Rt), .in2({5{1'b0}}), .out(DA), .sel(S_DA));  // open: in3
  Multiplexer #(.select(2), .width(32), .enable("false")) multiplexer_3 (
    .in0(ALU_Out), .in1(Special_Ins_Data), .in2(Lo), .in3(Hi), .out(DATA_INPUT), .sel(S_DATA_IN));
  ProgramCounter programcounter_1 (
    .jmp_addr(jmp_address), .jmp_Jump(Jmp), .rst_Reset(reset), .Q(PC_Addrs), .fetch(fetch));
  Branch_Control branch_control_1 (
    .JS_Jump_Size(Const_extended), .IA_InstructionAddress(PC_Addrs), .jmp(Jmp), .FC(FC),
    .NIR_NextInstructionAddrs(NI));
  assign Const_extended = {{16{1'b0}}, Const};  // Bit_Extender bit_extender_1
  assign JS = {{16{1'b0}}, Const};  // Bit_Extender bit_extender_2
  InstructionDecoder instructiondecoder_1 (
    .Instruction(Instruction), .DA_DataAddress(DA), .R_W_ReadWrite(R_W), .SA_SelectorA(SA),
    .SB_SelectorB(Rt), .Jmp(Jmp), .FC_FlagCondition(FC), .dest(dest), .A(Const), .Op(Op), .Load(Load),
    .Store(Store), .Active_EI(EI), .EspecialInstruction(Esp_Ins_S), .Read_Hi_Lo(R_Hi_Lo), .mf_Hi_Lo(mf_Hi_Lo));
  Multiplexer #(.select(2), .width(32), .enable("false")) multiplexer_4 (
    .in0(B), .in1(Const_extended), .in2({32{1'b0}}), .out(B_prime), .sel(S_ALUB));  // open: in3
  Multiplexer #(.width(32), .enable("false")) multiplexer_5 (.in0(B), .in1(JS), .out(B_prime), .sel(comparator_1_eq));
  Comparator #(.width(32), .mode("unsigned")) comparator_1 (
    .a(B), .b({32{1'b0}}), .eq(comparator_1_eq));  // open: gt, lt
  Special_Op_Unit special_op_unit_1 (
    .Enable(EI), .EspIns_Selector(Esp_Ins_S), .RS_Data({A, TTY_Data}), .KBD_Data(KBD_Data),
    .KBD_Enable(KBD_En), .Halt(halt), .TTY_DATA(TTY_Data_t), .TTY_Enable(TTY_Enable),
    .Write_Data(W_SOU_Data), .RD_Data(SOU_Data));
  Multiplexer #(.width(32), .enable("false")) multiplexer_6 (
    .in0(DATA_IN), .in1(DATA_HI_LO), .out(multiplexer_6_out), .sel(mf_Hi_Lo));
  RegisterFile registerfile_1 (
    .DA_DestinationAddress(DA), .DI_DataInput(DATA_INPUT), .RW_Read_Write(R_W), .Rst_Reset(reset), .SA(SA),
    .SB(SB), .Out_A({A, TTY_Data}), .Out_B(B));
  Multiplexer #(.select(3), .enable("false")) multiplexer_7 (
    .in0(1'b0), .in1(A___B_signed), .in2(A___B_unsigned), .in3(A____B), .in4(A___B_signed_t), .in5(A____B_t),
    .out(FC), .sel(S_FlagCondition));  // open: in6, in7
  Multiplexer #(.select(2), .width(32), .enable("false")) multiplexer_8 (
    .in0(NI), .in1({A, TTY_Data}), .in2({PC_Addrs[31:28], dest, 2'b00}), .out(jmp_address),
    .sel(S_jmp_address));  // open: in3
  Multiplexer #(.width(32), .enable("false")) multiplexer_9 (
    .in0(multiplexer_6_out), .in1(SOU_Data), .out(DATA_INPUT), .sel(W_SOU_Data));
  ALU alu_1 (
    .A({A, TTY_Data}), .B(B_prime), .Op(Op), .HI_CONTENT(DATA_HI), .UPDATE_HI_LO(Upd_Hi), .Output(ALU_Out),
    .LO_CONTENT(DATA_LO), .B_ZERO(B_Cero));  // open: A___B_unsigned, A___B_signed, A____B, A____B_2, A___B_s
  Hi_Lo_registers_Finished__main main_1 (
    .HI_Content(DATA_HI), .Lo_Content(DATA_LO), .Update(UpdateHi), .Reset(reset), .Read_HI_Lo(R_Hi_Lo),
    .HI_Lo_Data(DATA_HI_LO));
  assign bit_extender_3_out = {{25{1'b0}}, KBD_Data};  // Bit_Extender bit_extender_3
  Random #(.width(32)) random_1 (.clk(clk), .next(1'b1), .out(random_1_out), .clr(reset));
  Multiplexer #(.width(32), .enable("false")) multiplexer_10 (
    .in0({32{1'b1}}), .in1(bit_extender_3_out), .out(multiplexer_10_out), .sel(KBD_Enable));
  Multiplexer #(.width(32), .enable("false")) multiplexer_11 (
    .in0(multiplexer_10_out), .in1(random_1_out), .out(Special_Ins_Data), .sel(S_SI));

  // Other names for the same wires on the sheet: A[6:0] = TTY_Data; final_dest[31:2] = {PC_Addrs[31:28], dest};
  //   PC[31:0] = PC_Addrs; Ins[31:0] = Instruction; KBD_Available = KBD_Enable; rst = reset;
  //   S_Special_Instruction = S_SI; TTY_En = TTY_Enable

  // Notes on the sheet:
  //   RegisterFile
  //   ALU
  //   MUX ENTRADAS
  //   Branch Contol
  //   Program Counter
  //   Esto se puede mejorar con un soplo multiplexor pero falta todavia un posible data input de hacer save word cuando tengamos MemoryMan vemos aca que hacemos
  //   Special Instruction Data Input
endmodule
