// Logisim project Hi_Lo_registers(Finished).circ as structural Verilog: 1 circuit, main circuit main
module main (
  input  [31:0] HI_Content,
  input  [31:0] Lo_Content,
  input  Update,
  input  Reset,
  output [31:0] HI_Data,
  output [31:0] Lo_Data
);

  wire clock_1_out;

  Clock clock_1 (.out(clock_1_out));
  Register #(.width(32)) Hi_Register (.D(HI_Content), .en(Update), .Q(HI_Data), .clk(clock_1_out), .clr(Reset));
  Register #(.width(32)) Lo_Register (.D(Lo_Content), .en(Update), .Q(Lo_Data), .clk(clock_1_out), .clr(Reset));
endmodule
