// Logisim project InstructionDecoder(Finished).circ as structural Verilog: 1 circuit, main circuit InstructionDecoder
module InstructionDecoder (
  input  [31:0] Instruction,
  output [4:0] DA_DataAddress,
  output [4:0] Rs,
  output [4:0] Rt,
  output [25:0] dest,
  output [15:0] OffSet,
  output [5:0] FuncCode,
  output [5:0] OpCode
);


  assign FuncCode = Instruction[5:0];
  assign OpCode = Instruction[31:26];
  assign Rs = Instruction[25:21];
  assign Rt = Instruction[20:16];

  // Other names for the same wires on the sheet: DA[4:0] = DA_DataAddress; X[4:0] = Instruction[10:6];
  //   RD[4:0] = Instruction[15:11]

  // Notes on the sheet:
  //   FuncCode
  //   OP-Code
  //   Input_Otput_Region
  //   RD
  //   Rt
  //   Rs
endmodule
