// Logisim project ProgramCounter(FInished).circ as structural Verilog: 1 circuit, main circuit ProgramCounter
module ProgramCounter (
  input  [31:0] jmp_addr,
  input  jmp_Jump,
  input  rst_Reset,
  output [31:0] Q
);

  wire clk_out;
  wire [31:0] adder_1_out, multiplexer_1_out;

  Clock clk (.out(clk_out));
  Register #(.width(32)) register_1 (.D(multiplexer_1_out), .en(1'b1), .Q(Q), .clk(clk_out), .clr(rst_Reset));
  Adder #(.width(32)) adder_1 (.a(Q), .b(32'h4), .out(adder_1_out));  // open: cin, cout
  Multiplexer #(.width(32), .enable("false")) multiplexer_1 (
    .in0(adder_1_out), .in1(jmp_addr), .out(multiplexer_1_out), .sel(jmp_Jump));
endmodule
